# Fritzing sketch gun_prototype (saved by Fritzing 0.9.4)

parts:
  Part1 = Breadboard Power Supply Board SMD
  BAT1 = BC9VPC [package=bc9vpc]
  S1 = Pushbutton [package="[THT]"]
  Part2 = KY-008 Laser Transmitter Module [package="Breakout board"]

nets:
  N1: Part1.VCC, S1.Pin_4
  N2: Part1.GND, BAT1.V-, Part2.-
  N3: Part1.VIN, BAT1.V+
  N4: S1.Pin_2, Part2.S

custom parts:
  KY-008 Laser Transmitter Module: Laser Transmitter module KY-008 for Arduino, emits a dot shaped red laser beam.
