# Fritzing sketch target_base_prototype (saved by Fritzing 0.9.4)
breadboards: 1

parts:
  Part1 = Arduino Uno (Rev3)
  J1 = Basic Servo
  LED1 = smd LED [color="Red (633nm)" package="0805 [SMD]"]
  R1 = PHOTOCELL [package=photocell]
  R2 = Resistor [tolerance=±2% resistance=10 package=THT]
  R3 = Resistor [tolerance=±5% resistance=220 package=THT]

nets:
  N1: Part1.A0, R1.P$2, R2.Pin_0
  N2: Part1.D4, R3.Pin_0
  N3: Part1.D7, J1.pulse
  5V: Part1.5V, J1.vcc, R1.P$1
  GND: Part1.GND, J1.gnd, LED1.anode, R2.Pin_1
  N4: LED1.cathode, R3.Pin_1
